// Logisim project 1.circ as structural Verilog
module alu (
  input  E,
  input  s,
  input  [3:0] A,
  input  [3:0] B,
  input  S0,
  input  S1,
  output [3:0] F,
  output COUT
);

  wire adder_4bit1_1_cout, adder_4bit4_1_cout, and_1_out;
  wire [3:0] adder_4bit1_1_s, adder_4bit4_1_s, andcirc_1_xandy, mux_2x1_4bit_1_f, notcirc_1_not_x;

  mux_2x1_4bit mux_2x1_4bit_1 (.E(E), .S(s), .X(A), .Y(B), .F(mux_2x1_4bit_1_f));
  notCirc notcirc_1 (.X(mux_2x1_4bit_1_f), .NOT_X(notcirc_1_not_x));
  andCirc andcirc_1 (.X(A), .Y(B), .XandY(andcirc_1_xandy));
  adder_4bit4 adder_4bit4_1 (.A(A), .B(B), .S(adder_4bit4_1_s), .COUT(adder_4bit4_1_cout));
  adder_4bit1 adder_4bit1_1 (.X(B), .S(adder_4bit1_1_s), .COUT(adder_4bit1_1_cout));
  mux_2x1_1bit mux_2x1_1bit_1 (
    .Bplus1(adder_4bit1_1_cout), .AplusB(adder_4bit4_1_cout), .S(and_1_out), .E(E), .F(COUT));
  mux_4x1_4bit mux_4x1_4bit_1 (
    .E(E), .NOT_X(notcirc_1_not_x), .aANDb(andcirc_1_xandy), .AplusB(adder_4bit4_1_s),
    .Bplus1(adder_4bit1_1_s), .S0(S0), .S1(S1), .F(F));
  and and_1 (and_1_out, S1, S0);
endmodule

module notCirc (
  input  [3:0] X,
  output [3:0] NOT_X
);

  not not_1 (NOT_X[0], X[0]);
  not not_2 (NOT_X[1], X[1]);
  not not_3 (NOT_X[2], X[2]);
  not not_4 (NOT_X[3], X[3]);
endmodule

module andCirc (
  input  [3:0] X,
  input  [3:0] Y,
  output [3:0] XandY
);

  and and_1 (XandY[0], X[0], Y[0]);
  and and_2 (XandY[1], X[1], Y[1]);
  and and_3 (XandY[2], X[2], Y[2]);
  and and_4 (XandY[3], X[3], Y[3]);
endmodule

module adder_4bit4 (
  input  [3:0] A,
  input  [3:0] B,
  output [3:0] S,
  output COUT
);

  wire fulladder_1_cout, fulladder_2_cout, fulladder_3_cout;

  fullAdder fulladder_1 (.A(A[0]), .B(B[0]), .CIN(1'b0), .S(S[0]), .COUT(fulladder_1_cout));
  fullAdder fulladder_2 (.A(A[1]), .B(B[1]), .CIN(fulladder_1_cout), .S(S[1]), .COUT(fulladder_2_cout));
  fullAdder fulladder_3 (.A(A[2]), .B(B[2]), .CIN(fulladder_2_cout), .S(S[2]), .COUT(fulladder_3_cout));
  fullAdder fulladder_4 (.A(A[3]), .B(B[3]), .CIN(fulladder_3_cout), .S(S[3]), .COUT(COUT));

  // Notes on the sheet:
  //   0bit
  //   1bit
  //   2bit
  //   3bit
endmodule

module adder_4bit1 (
  input  [3:0] X,
  output [3:0] S,
  output COUT
);

  adder_4bit4 adder_4bit4_1 (.A(X), .B(4'b0001), .S(S), .COUT(COUT));
endmodule

module mux_2x1_1bit (
  input  E,
  input  AplusB,
  input  Bplus1,
  input  S,
  output F
);

  wire and_1_out, and_2_out, not_1_out;

  not not_1 (not_1_out, S);
  and and_1 (and_1_out, AplusB, not_1_out, E);
  and and_2 (and_2_out, Bplus1, S, E);
  or or_1 (F, and_1_out, and_2_out);
endmodule

module mux_2x1_4bit (
  input  E,
  input  [3:0] X,
  input  [3:0] Y,
  input  S,
  output [3:0] F
);

  wire and_1_out, and_2_out, and_3_out, and_4_out, and_5_out, and_6_out, and_7_out, and_8_out, not_1_out;

  not not_1 (not_1_out, S);
  and and_1 (and_1_out, X[0], not_1_out, E);
  and and_2 (and_2_out, X[1], not_1_out, E);
  and and_3 (and_3_out, X[2], not_1_out, E);
  and and_4 (and_4_out, X[3], not_1_out, E);
  and and_5 (and_5_out, Y[0], S, E);
  and and_6 (and_6_out, Y[1], S, E);
  and and_7 (and_7_out, Y[2], S, E);
  and and_8 (and_8_out, Y[3], S, E);
  or or_1 (F[0], and_1_out, and_5_out);
  or or_2 (F[1], and_2_out, and_6_out);
  or or_3 (F[2], and_3_out, and_7_out);
  or or_4 (F[3], and_4_out, and_8_out);
endmodule

module mux_4x1_4bit (
  input  E,
  input  [3:0] NOT_X,
  input  [3:0] aANDb,
  input  [3:0] AplusB,
  input  S1,
  input  [3:0] Bplus1,
  input  S0,
  output [3:0] F
);

  wire [3:0] mux_2x1_4bit_1_f, mux_2x1_4bit_2_f;

  mux_2x1_4bit mux_2x1_4bit_1 (.E(E), .S(S0), .X(NOT_X), .Y(AplusB), .F(mux_2x1_4bit_1_f));
  mux_2x1_4bit mux_2x1_4bit_2 (.E(E), .S(S0), .X(aANDb), .Y(Bplus1), .F(mux_2x1_4bit_2_f));
  mux_2x1_4bit mux_2x1_4bit_3 (.E(E), .S(S1), .X(mux_2x1_4bit_1_f), .Y(mux_2x1_4bit_2_f), .F(F));
endmodule

module halfAdder (
  input  A,
  input  B,
  output S,
  output COUT
);

  xor xor_1 (S, A, B);
  and and_1 (COUT, A, B);
endmodule

module fullAdder (
  input  A,
  input  B,
  input  CIN,
  output S,
  output COUT
);

  wire halfadder_1_cout, halfadder_1_s, halfadder_2_cout;

  halfAdder halfadder_1 (.A(A), .B(B), .S(halfadder_1_s), .COUT(halfadder_1_cout));
  halfAdder halfadder_2 (.A(halfadder_1_s), .B(CIN), .S(S), .COUT(halfadder_2_cout));
  or or_1 (COUT, halfadder_2_cout, halfadder_1_cout);
endmodule
