// Logisim project 2.circ as structural Verilog
module counter_4bit (
);

  wire clock_1_out, nand_1_out, not_1_out, not_2_out, not_3_out, not_4_out, not_5_out, not_6_out, not_7_out,
       not_8_out, not_9_out, not_10_out, not_11_out, not_12_out, t_ff_1_q, t_ff_2_q, t_ff_3_q, t_ff_4_q;

  Clock clock_1 (.out(clock_1_out));
  not not_1 (not_1_out, clock_1_out);
  not not_2 (not_2_out, 1'b1);
  T_Flip_Flop t_ff_1 (.T(1'b1), .clk(not_1_out), .Q(t_ff_1_q), .reset(not_3_out), .preset(not_2_out));  // open: Qn
  not not_3 (not_3_out, nand_1_out);
  not not_4 (not_4_out, 1'b1);
  T_Flip_Flop t_ff_2 (.T(1'b1), .clk(not_5_out), .Q(t_ff_2_q), .reset(not_6_out), .preset(not_4_out));  // open: Qn
  not not_5 (not_5_out, t_ff_1_q);
  not not_6 (not_6_out, nand_1_out);
  not not_7 (not_7_out, 1'b1);
  T_Flip_Flop t_ff_3 (.T(1'b1), .clk(not_8_out), .Q(t_ff_3_q), .reset(not_9_out), .preset(not_7_out));  // open: Qn
  not not_8 (not_8_out, t_ff_2_q);
  not not_9 (not_9_out, nand_1_out);
  T_Flip_Flop t_ff_4 (.T(1'b1), .clk(not_10_out), .Q(t_ff_4_q), .reset(not_12_out), .preset(not_11_out));  // open: Qn
  not not_10 (not_10_out, t_ff_3_q);
  not not_11 (not_11_out, 1'b1);
  not not_12 (not_12_out, nand_1_out);
  nand nand_1 (nand_1_out, t_ff_1_q, t_ff_4_q);
endmodule
