// Logisim project erg1_2.circ as structural Verilog: 1 circuit, main circuit main
module main (
  input  x,
  input  y,
  input  z,
  output f
);

  wire and_1_out, and_2_out, and_3_out;

  and and_1 (and_1_out, y, z);
  and and_2 (and_2_out, x, z);
  or or_1 (f, and_1_out, and_2_out, and_3_out);
  and and_3 (and_3_out, x, y);

  // Notes on the sheet:
  //   F = XY + YZ + XZ
endmodule
