// Logisim project adders.circ as structural Verilog
module half_adder_1bit (
  input  X,
  input  Y,
  output S,
  output Cout
);

  xor xor_1 (S, X, Y);
  and and_1 (Cout, X, Y);
endmodule

module full_adder_1bit (
  input  A,
  input  B,
  input  Cin,
  output S,
  output Cout
);

  wire half_adder_1bit_1_cout, half_adder_1bit_1_s, half_adder_1bit_2_cout;

  half_adder_1bit half_adder_1bit_1 (.X(A), .Y(B), .S(half_adder_1bit_1_s), .Cout(half_adder_1bit_1_cout));
  half_adder_1bit half_adder_1bit_2 (.X(half_adder_1bit_1_s), .Y(Cin), .S(S), .Cout(half_adder_1bit_2_cout));
  or or_1 (Cout, half_adder_1bit_2_cout, half_adder_1bit_1_cout);
endmodule

module full_adder_4bit (
  input  Cin,
  input  [3:0] X,
  input  [3:0] Y,
  output [3:0] S,
  output Cout
);

  wire full_adder_1bit_1_cout, full_adder_1bit_2_cout, full_adder_1bit_3_cout;

  full_adder_1bit full_adder_1bit_1 (.A(X[0]), .B(Y[0]), .Cin(Cin), .S(S[0]), .Cout(full_adder_1bit_1_cout));
  full_adder_1bit full_adder_1bit_2 (
    .A(X[1]), .B(Y[1]), .Cin(full_adder_1bit_1_cout), .S(S[1]), .Cout(full_adder_1bit_2_cout));
  full_adder_1bit full_adder_1bit_3 (
    .A(X[2]), .B(Y[2]), .Cin(full_adder_1bit_2_cout), .S(S[2]), .Cout(full_adder_1bit_3_cout));
  full_adder_1bit full_adder_1bit_4 (.A(X[3]), .B(Y[3]), .Cin(full_adder_1bit_3_cout), .S(S[3]), .Cout(Cout));
endmodule

module full_adder_16bit (
  input  Cin,
  input  [15:0] X,
  input  [15:0] Y,
  output [15:0] S,
  output Cout
);

  wire full_adder_4bit_1_cout, full_adder_4bit_2_cout, full_adder_4bit_3_cout;

  full_adder_4bit full_adder_4bit_1 (.Cin(Cin), .X(X[3:0]), .Y(Y[3:0]), .S(S[3:0]), .Cout(full_adder_4bit_1_cout));
  full_adder_4bit full_adder_4bit_2 (
    .Cin(full_adder_4bit_1_cout), .X(X[7:4]), .Y(Y[7:4]), .S(S[7:4]), .Cout(full_adder_4bit_2_cout));
  full_adder_4bit full_adder_4bit_3 (
    .Cin(full_adder_4bit_2_cout), .X(X[11:8]), .Y(Y[11:8]), .S(S[11:8]), .Cout(full_adder_4bit_3_cout));
  full_adder_4bit full_adder_4bit_4 (
    .Cin(full_adder_4bit_3_cout), .X(X[15:12]), .Y(Y[15:12]), .S(S[15:12]), .Cout(Cout));
  Hex_Digit_Display hex_digit_display_1 (.value(S[15:12]));  // open: dp
  Hex_Digit_Display hex_digit_display_2 (.value(S[7:4]));  // open: dp
  Hex_Digit_Display hex_digit_display_3 (.value(S[11:8]));  // open: dp
  Hex_Digit_Display hex_digit_display_4 (.value(S[3:0]));  // open: dp
endmodule

module full_adder_32bit (
  input  [31:0] X,
  input  Cin,
  input  [31:0] Y,
  output [31:0] out_4,
  output Cout
);

  wire full_adder_16bit_1_cout;

  Hex_Digit_Display hex_digit_display_1 (.value(out_4[31:28]));  // open: dp
  Hex_Digit_Display hex_digit_display_2 (.value(out_4[27:24]));  // open: dp
  full_adder_16bit full_adder_16bit_1 (
    .Cin(Cin), .X(X[15:0]), .Y(Y[15:0]), .S(out_4[15:0]), .Cout(full_adder_16bit_1_cout));
  full_adder_16bit full_adder_16bit_2 (
    .Cin(full_adder_16bit_1_cout), .X(X[31:16]), .Y(Y[31:16]), .S(out_4[31:16]), .Cout(Cout));
  Hex_Digit_Display hex_digit_display_3 (.value(out_4[23:20]));  // open: dp
  Hex_Digit_Display hex_digit_display_4 (.value(out_4[19:16]));  // open: dp
  Hex_Digit_Display hex_digit_display_5 (.value(out_4[15:12]));  // open: dp
  Hex_Digit_Display hex_digit_display_6 (.value(out_4[7:4]));  // open: dp
  Hex_Digit_Display hex_digit_display_7 (.value(out_4[11:8]));  // open: dp
  Hex_Digit_Display hex_digit_display_8 (.value(out_4[3:0]));  // open: dp
endmodule
