// Logisim project decoders.circ as structural Verilog
module decoder_2x4 (
  input  X,
  input  Y,
  input  E,
  output D0,
  output D1,
  output D2,
  output D3
);

  wire not_1_out, not_2_out;

  not not_1 (not_1_out, X);
  and and_1 (D0, not_1_out, not_2_out, E);
  and and_2 (D1, not_1_out, Y, E);
  and and_3 (D2, X, not_2_out, E);
  not not_2 (not_2_out, Y);
  and and_4 (D3, X, Y, E);
endmodule

module decoder_3x8 (
  input  E,
  input  X,
  input  Y,
  input  Z,
  output D0,
  output D2,
  output D4,
  output D6,
  output D1,
  output D3,
  output D5,
  output D7
);

  wire decoder_2x4_1_d0, decoder_2x4_1_d1, decoder_2x4_1_d2, decoder_2x4_1_d3, decoder_2x4_2_d0,
       decoder_2x4_2_d1, decoder_2x4_2_d2, decoder_2x4_2_d3, not_1_out;

  not not_1 (not_1_out, Z);
  decoder_2x4 decoder_2x4_1 (
    .X(X), .Y(Y), .E(not_1_out), .D0(decoder_2x4_1_d0), .D1(decoder_2x4_1_d1), .D2(decoder_2x4_1_d2),
    .D3(decoder_2x4_1_d3));
  decoder_2x4 decoder_2x4_2 (
    .X(X), .Y(Y), .E(Z), .D0(decoder_2x4_2_d0), .D1(decoder_2x4_2_d1), .D2(decoder_2x4_2_d2),
    .D3(decoder_2x4_2_d3));
  and and_1 (D0, decoder_2x4_1_d0, E);
  and and_2 (D2, decoder_2x4_1_d1, E);
  and and_3 (D4, decoder_2x4_1_d2, E);
  and and_4 (D6, decoder_2x4_1_d3, E);
  and and_5 (D1, decoder_2x4_2_d0, E);
  and and_6 (D3, decoder_2x4_2_d1, E);
  and and_7 (D5, decoder_2x4_2_d2, E);
  and and_8 (D7, decoder_2x4_2_d3, E);
endmodule

module decoder_4x16 (
  input  E,
  input  X,
  input  Y,
  input  Z,
  input  W,
  output D0,
  output D2,
  output D4,
  output D6,
  output D8,
  output D10,
  output D12,
  output D14,
  output D1,
  output D3,
  output D5,
  output D7,
  output D9,
  output D11,
  output D13,
  output D15
);

  wire decoder_3x8_1_d0, decoder_3x8_1_d1, decoder_3x8_1_d2, decoder_3x8_1_d3, decoder_3x8_1_d4,
       decoder_3x8_1_d5, decoder_3x8_1_d6, decoder_3x8_1_d7, decoder_3x8_2_d0, decoder_3x8_2_d1,
       decoder_3x8_2_d2, decoder_3x8_2_d3, decoder_3x8_2_d4, decoder_3x8_2_d5, decoder_3x8_2_d6,
       decoder_3x8_2_d7, not_1_out;

  not not_1 (not_1_out, W);
  decoder_3x8 decoder_3x8_1 (
    .X(X), .Y(Y), .Z(Z), .E(not_1_out), .D2(decoder_3x8_1_d2), .D4(decoder_3x8_1_d4), .D6(decoder_3x8_1_d6),
    .D1(decoder_3x8_1_d1), .D3(decoder_3x8_1_d3), .D5(decoder_3x8_1_d5), .D7(decoder_3x8_1_d7),
    .D0(decoder_3x8_1_d0));
  decoder_3x8 decoder_3x8_2 (
    .X(X), .Y(Y), .Z(Z), .E(W), .D2(decoder_3x8_2_d2), .D4(decoder_3x8_2_d4), .D6(decoder_3x8_2_d6),
    .D1(decoder_3x8_2_d1), .D3(decoder_3x8_2_d3), .D5(decoder_3x8_2_d5), .D7(decoder_3x8_2_d7),
    .D0(decoder_3x8_2_d0));
  and and_1 (D0, decoder_3x8_1_d0, E);
  and and_2 (D2, decoder_3x8_1_d1, E);
  and and_3 (D4, decoder_3x8_1_d2, E);
  and and_4 (D6, decoder_3x8_1_d3, E);
  and and_5 (D8, decoder_3x8_1_d4, E);
  and and_6 (D10, decoder_3x8_1_d5, E);
  and and_7 (D12, decoder_3x8_1_d6, E);
  and and_8 (D14, decoder_3x8_1_d7, E);
  and and_9 (D1, decoder_3x8_2_d0, E);
  and and_10 (D3, decoder_3x8_2_d1, E);
  and and_11 (D5, decoder_3x8_2_d2, E);
  and and_12 (D7, decoder_3x8_2_d3, E);
  and and_13 (D9, decoder_3x8_2_d4, E);
  and and_14 (D11, decoder_3x8_2_d5, E);
  and and_15 (D13, decoder_3x8_2_d6, E);
  and and_16 (D15, decoder_3x8_2_d7, E);
endmodule
