// Logisim project multiplexer.circ as structural Verilog
module multiplexer_2x1 (
  input  S,
  input  [7:0] X,
  input  [7:0] Y,
  input  E,
  output [7:0] out_5
);

  wire and_1_out, and_2_out, and_3_out, and_4_out, and_5_out, and_6_out, and_7_out, and_8_out, and_9_out,
       and_10_out, and_11_out, and_12_out, and_13_out, and_14_out, and_15_out, and_16_out, not_1_out;

  not not_1 (not_1_out, S);
  and and_1 (and_1_out, X[0], not_1_out, E);
  and and_2 (and_2_out, X[1], not_1_out, E);
  and and_3 (and_3_out, X[2], not_1_out, E);
  and and_4 (and_4_out, X[3], not_1_out, E);
  and and_5 (and_5_out, X[4], not_1_out, E);
  and and_6 (and_6_out, X[5], not_1_out, E);
  and and_7 (and_7_out, X[6], not_1_out, E);
  and and_8 (and_8_out, X[7], not_1_out, E);
  and and_9 (and_9_out, Y[0], S, E);
  and and_10 (and_10_out, Y[1], S, E);
  and and_11 (and_11_out, Y[2], S, E);
  and and_12 (and_12_out, Y[3], S, E);
  and and_13 (and_13_out, Y[4], S, E);
  and and_14 (and_14_out, Y[5], S, E);
  and and_15 (and_15_out, Y[6], S, E);
  and and_16 (and_16_out, Y[7], S, E);
  or or_1 (out_5[0], and_1_out, and_9_out);
  or or_2 (out_5[1], and_2_out, and_10_out);
  or or_3 (out_5[2], and_3_out, and_11_out);
  or or_4 (out_5[3], and_4_out, and_12_out);
  or or_5 (out_5[4], and_5_out, and_13_out);
  or or_6 (out_5[5], and_6_out, and_14_out);
  or or_7 (out_5[6], and_7_out, and_15_out);
  or or_8 (out_5[7], and_8_out, and_16_out);
endmodule
