// Logisim project compare.circ as structural Verilog
module compare_1bit (
  input  in_1,
  input  in_2,
  output B_Bigger,
  output Both,
  output A_Bigger
);

  wire not_1_out, not_2_out;

  not not_1 (not_1_out, in_1);
  and and_1 (B_Bigger, not_1_out, in_2);
  and and_2 (A_Bigger, in_1, not_2_out);
  not not_2 (not_2_out, in_2);
  xnor xnor_1 (Both, in_1, in_2);
endmodule

module compare_2bits (
  input  [1:0] A,
  input  [1:0] B,
  output Same,
  output A_Bigger,
  output B_Bigger
);

  wire and_2_out, compare_1bit_1_b_bigger, compare_1bit_1_both, compare_1bit_2_b_bigger, compare_1bit_2_both;

  compare_1bit compare_1bit_1 (
    .in_1(A[0]), .in_2(B[0]), .B_Bigger(compare_1bit_1_b_bigger), .Both(compare_1bit_1_both));  // open: A_Bigger
  compare_1bit compare_1bit_2 (
    .in_1(A[1]), .in_2(B[1]), .B_Bigger(compare_1bit_2_b_bigger), .Both(compare_1bit_2_both));  // open: A_Bigger
  and and_1 (Same, compare_1bit_1_both, compare_1bit_2_both);
  and and_2 (and_2_out, compare_1bit_2_both, compare_1bit_1_b_bigger);
  or or_1 (B_Bigger, compare_1bit_2_b_bigger, and_2_out);
  nor nor_1 (A_Bigger, Same, B_Bigger);
endmodule

module compare_4bits (
  input  [3:0] A,
  input  [3:0] B,
  output Same,
  output A_Bigger,
  output B_Bigger
);

  wire and_2_out, compare_2bits_1_b_bigger, compare_2bits_1_same, compare_2bits_2_b_bigger,
       compare_2bits_2_same;

  compare_2bits compare_2bits_1 (
    .A(A[1:0]), .B(B[1:0]), .Same(compare_2bits_1_same), .B_Bigger(compare_2bits_1_b_bigger));  // open: A_Bigger
  compare_2bits compare_2bits_2 (
    .A(A[3:2]), .B(B[3:2]), .Same(compare_2bits_2_same), .B_Bigger(compare_2bits_2_b_bigger));  // open: A_Bigger
  and and_1 (Same, compare_2bits_1_same, compare_2bits_2_same);
  and and_2 (and_2_out, compare_2bits_2_same, compare_2bits_1_b_bigger);
  or or_1 (B_Bigger, compare_2bits_2_b_bigger, and_2_out);
  nor nor_1 (A_Bigger, Same, B_Bigger);
endmodule
